# Fritzing sketch thermostat_nodemcu (saved by Fritzing 0.9.3b)
stripboards: 1
breadboards: 1

parts:
  KY-1 = Keyes Relay [package=THT]
  Q4 = NPN-Transistor [package="TO92 [THT]"]
  R3 = Resistor [tolerance=±5% resistance=10k package=THT]
  R4 = Resistor [tolerance=±5% resistance=10k package=THT]
  DS1 = DS18B20 1-Wire Temperature Sensor [part_number=DS18B20]
  R5 = Resistor [tolerance=±5% resistance=4.7k package=THT]
  U3 = NodeMCU V3.0

nets:
  N1: KY-1.signal, Q4.C, R4.Pin_0
  N2: KY-1.power, R4.Pin_1, U3.VU
  N3: KY-1.ground, Q4.E, U3.GND#41
  N4: Q4.B, R3.Pin_0
  N5: R3.Pin_1, U3.D1
  N6: DS1.GND, R5.Pin_1, U3.GND#6, U3.GND#13, U3.GND#16, U3.GND#33
  N7: DS1.DQ, R5.Pin_0, U3.D2
  VDD: DS1.VDD, U3.3V3

custom parts:
  Keyes Relay: The Keyes 5V relay module is suitable for SCM development, home appliance control. It uses a 5V~12V TIL control signal which can control DC / AC signal.
  NodeMCU V3.0: ESP8266 based NodeMCU
